# Fritzing sketch circuit (saved by Fritzing 0.9.3b)
breadboards: 1

parts:
  R1 = Resistor [tolerance=±5% resistance=220 package=THT]
  Raspberry_Pi_1 = Raspberry Pi 3 [part_number=RPI-3-V1.2]
  LED2 = RGB LED (com. cathode, rbg) [package="5 mm [THT]"]
  R2 = Resistor [tolerance=±5% resistance=220 package=THT]
  R3 = Resistor [tolerance=±5% resistance=220 package=THT]

nets:
  N1: R1.Pin_0, Raspberry_Pi_1.GIPO18
  N2: R1.Pin_1, LED2.red_anode
  N3: Raspberry_Pi_1.GIPO24, R2.Pin_0
  N4: Raspberry_Pi_1.GIPO23, R3.Pin_0
  N5: Raspberry_Pi_1.GND, LED2.common_cathode
  N6: LED2.blue_anode, R2.Pin_1
  N7: LED2.green_anode, R3.Pin_1
