# Fritzing sketch circuit (saved by Fritzing 0.9.3b)

parts:
  元件1 = FTDI Basic Programmer
  Raspberry_Pi_1 = Raspberry Pi 3 [part_number=RPI-3-V1.2]

nets:
  N1: 元件1.RXI, Raspberry_Pi_1.GIPO14
  N2: 元件1.TXO, Raspberry_Pi_1.GIPO15
  GND: 元件1.GND, Raspberry_Pi_1.GND
